# Fritzing sketch activLoad (saved by Fritzing 0.9.3b)
breadboards: 1

parts:
  R1 = Resistor [tolerance=±5% resistance=100 package=THT]
  Часть1 = Arduino Uno (Rev3)
  R2 = Resistor [tolerance=±5% resistance=10k package=THT]
  D1 = Rectifier Diode [part_number=1N4001 package="300 mil [THT]"]
  Q1 = MOSFET-NCHANNEL [package=to220v]
  M1 = DC Motor

nets:
  N1: R1.Pin_0, Часть1.D7
  N2: R1.Pin_1, R2.Pin_1, Q1.G
  N3: Часть1.GND, R2.Pin_0, Q1.S
  N4: D1.cathode, M1.pin_2
  N5: D1.anode, Q1.D, M1.pin_1
