# Fritzing sketch lightSensor (saved by Fritzing 0.9.3b)
breadboards: 1

parts:
  Часть1 = Arduino Uno (Rev3)
  R1 = Photocell (LDR) [package=THT]
  LED1 = LED - 5mm [color="Red (633nm)" package="5 mm [THT]"]
  R3 = Resistor [tolerance=±5% resistance=220 package=THT]

nets:
  N1: Часть1.A0, R1.pin_1
  N2: Часть1.D5_PWM, LED1.cathode, R3.Pin_1
  N3: Часть1.GND, R1.pin_0

// code stored in the sketch: lightSensor.ino
#define MIN_LUM 1
#define MAX_LUM 3
#define pinPhoto A0
#define pinLamp 13

int raw;


void setup() {
	raw=0;
  Serial.begin(9600);
  pinMode( pinPhoto, INPUT );
	pinMode( pinLamp, INPUT );
}

void loop() {
  raw = analogRead( pinPhoto );
    if ( raw <= MIN_LUM )
    {
	// 
			digitalWrite(pinLamp, HIGH);
			delay(1000);
    }
		else if ( raw > MAX_LUM )
		{
	// 
			digitalWrite(pinLamp, LOW);
			deplay(1000);
		}
  Serial.println( raw );
  delay(200);
}
