# Fritzing sketch main (saved by Fritzing 0.9.3b)
breadboards: 1

parts:
  Часть1 = Arduino Uno (Rev3)
  ZS-042_RTC1 = ZS-042 RTC Module
  D1 = SOLAR-IXYS [package=solarbit-12x1]
  KY-1 = Keyes Relay [package=THT]
  KY-2 = Keyes Relay [package=THT]
  KY-3 = Keyes Relay [package=THT]
  M2 = DC Motor
  LM1 = RioRand LM2596
  LM2 = RioRand LM2596
  J1 = screw terminal, 3 pins  # not connected
  J2 = screw terminal, 3 pins  # not connected
  J3 = screw terminal, 3 pins
  J4 = screw terminal, 3 pins
  M1 = DC Motor
  J5 = screw terminal, 3 pins
  LED1 = LEDs [package=led-1206]  # not connected
  RHT1 = Humidity and Temperature Sensor RHT03  # not connected

nets:
  N1: Часть1.A1, D1.C, J5.pin2
  N2: Часть1.A4/SDA, ZS-042_RTC1.SDA
  N3: Часть1.A5/SCL, ZS-042_RTC1.SCL
  GND: Часть1.GND, ZS-042_RTC1.GND, LM1.Pin_3, J5.pin3
  N4: ZS-042_RTC1.VCC, LM1.Pin_2
  N5: KY-1.NC, KY-2.NC, KY-3.NC, LM2.Pin_2
  N6: KY-1.C, J4.pin2, M1.pin_2
  N7: KY-2.C, M2.pin_2, J3.pin1
  N8: KY-3.C, J3.pin3
  N9: LM2.Pin_3, J3.pin2, J4.pin1, J4.pin3

custom parts:
  Keyes Relay: The Keyes 5V relay module is suitable for SCM development, home appliance control. It uses a 5V~12V TIL control signal which can control DC / AC signal.
