# Fritzing sketch timer (saved by Fritzing 0.9.3b)
breadboards: 1

parts:
  Часть1 = Arduino Uno (Rev3)
  ZS-042_RTC1 = ZS-042 RTC Module

nets:
  N1: Часть1.A4/SDA, ZS-042_RTC1.SDA
  N2: Часть1.A5/SCL, ZS-042_RTC1.SCL
  5V: Часть1.5V, ZS-042_RTC1.VCC
  GND: Часть1.GND, ZS-042_RTC1.GND

// code stored in the sketch: timer.ino
time.begin(RTC_DS3231);
time.begin(RTC_DS3231);

void setup()
{
	
}

void loop()
{
	
}
